// Logisim project Circuit.circ as structural Verilog: 2 circuits, main circuit main
module main (
  input  in_1,
  input  [3:0] in_2,
  input  in_3,
  input  in_4
);

  wire ABC, and_1_out, and_2_out, button_1_out, button_5_out, Clock_Pulse, CLR_KB, CLR_MR, CLR_P, CLS,
       counter_4_carry, keyboard_1_avail, LOAD, not_1_out, not_2_out, not_3_out, not_4_out, or_1_out,
       or_2_out, RESET, SAVE;
  wire [3:0] counter_2_q, counter_2_q_2, register_1_q, register_1_q_2;
  wire [4:0] opearation_1_result, opearation_2_result;
  wire [6:0] keyboard_1_data, multiplexer_2_out, ram_1_data;
  wire [7:0] counter_1_q, counter_3_q, multiplexer_1_out;
  wire [15:0] ram_2_data;

  Clock clock_1 (.out(Clock_Pulse));
  Keyboard keyboard_1 (.clk(Clock_Pulse), .clr(CLR_KB), .avail(keyboard_1_avail), .data(keyboard_1_data));  // open: re
  and and_1 (and_1_out, Clock_Pulse, keyboard_1_avail);
  Button button_1 (.out(button_1_out));
  and and_2 (and_2_out, Clock_Pulse, keyboard_1_avail);
  Button button_2 (.out(RESET));
  Hex_Digit_Display hex_digit_display_1 (.value(register_1_q_2));  // open: dp
  Counter counter_1 (.Q(counter_1_q), .clk(and_1_out), .clr(button_1_out));  // open: load, D, count, carry
  Button button_3 (.out(SAVE));
  Hex_Digit_Display hex_digit_display_2 (.value(register_1_q));  // open: dp
  Register register_1 (.D(counter_1_q), .Q({register_1_q_2, register_1_q}), .clk(RESET));  // open: en, clr
  Opearation opearation_1 (.Input(keyboard_1_data[5:1]), .Sel(1'b0), .Result(opearation_1_result));
  Hex_Digit_Display hex_digit_display_3 (.value(counter_2_q_2));  // open: dp
  Counter counter_2 (.Q({counter_2_q_2, counter_2_q}), .clk(and_1_out), .clr(RESET));  // open: load, D, count, carry
  Hex_Digit_Display hex_digit_display_4 (.value(counter_2_q));  // open: dp
  Multiplexer #(.width(8), .enable("false")) multiplexer_1 (
    .in0(counter_1_q), .in1(counter_3_q), .out(multiplexer_1_out), .sel(in_1));
  not not_1 (not_1_out, in_1);
  not not_2 (not_2_out, or_1_out);
  or or_1 (or_1_out, in_1, in_3);
  RAM #(.dataWidth(7), .bus("separate")) ram_1 (
    .addr(multiplexer_1_out), .din({keyboard_1_data[6], opearation_1_result, keyboard_1_data[0]}),
    .data(ram_1_data), .str(not_1_out), .clk(and_2_out), .ld(in_1), .clr(CLR_MR));  // open: sel
  Button button_4 (.out(LOAD));
  RAM #(.addrWidth(4), .dataWidth(16), .bus("separate")) ram_2 (
    .addr(in_2), .din({register_1_q_2, register_1_q, counter_2_q_2, counter_2_q}), .data(ram_2_data),
    .str(not_2_out), .clk(SAVE), .ld(or_1_out), .clr(CLR_P));  // open: sel
  not not_3 (not_3_out, in_1);
  Counter counter_3 (
    .load(not_3_out), .D(ram_2_data[15:8]), .count(in_1), .Q(counter_3_q), .clk(or_2_out), .clr(button_5_out));  // open: carry
  Counter #(.ongoal("stay")) counter_4 (
    .load(1'b1), .D(ram_2_data[7:0]), .count(in_1), .carry(counter_4_carry), .clk(or_2_out),
    .clr(button_5_out));  // open: Q
  or or_2 (or_2_out, ABC, LOAD);
  Opearation opearation_2 (.Input(ram_1_data[5:1]), .Sel(1'b1), .Result(opearation_2_result));
  not not_4 (not_4_out, counter_4_carry);
  Button button_5 (.out(button_5_out));
  Multiplexer #(.width(7), .enable("false")) multiplexer_2 (
    .in0({ram_1_data[6], opearation_2_result, ram_1_data[0]}), .in1(ram_1_data), .out(multiplexer_2_out),
    .sel(in_4));
  and and_3 (ABC, not_4_out, in_1, Clock_Pulse);
  TTY tty_1 (.data(multiplexer_2_out), .clk(ABC), .clr(CLS));  // open: we
  Button button_6 (.out(CLS));
  Button button_7 (.out(CLR_KB));
  Button button_8 (.out(CLR_MR));
  Button button_9 (.out(CLR_P));

  // Other names for the same wires on the sheet: DIS = in_4; E___D = in_1; SEL[3:0] = in_2; X = in_3

  // Notes on the sheet:
  //   1) Set [E / D] to 0
  //   Data Encryption
  //   2) Reset PIN using RESET button
  //   3) Enter Your Data in Message Keyboard
  //   4) Trigger The Clock Pulse (Ctrl + k)
  //   - Encrypted data will be stored in Memory
  //   5) Press SAVE Button to save your PIN
  //   A
  //   - And Unique PIN for decryption is provided in Display
  //   4) After PIN is loaded set X to 0
  //   5) Set Value of DIS to
  //   Data Decryption
  //   1) Set [E / D] to 0 , And turn off the clock pulse
  //   2) Select your PIN from storage using SEL bits
  //   3) To load PIN set X to 1 And Press LOAD button
  //   - 0 for Decrypted data
  //   - 1 for Encrypted Message
  //   6) For display set [ E / D ] to 1 And Trigger the Clock Pulse
  //   A
endmodule

module Opearation (
  input  [4:0] Input,
  input  Sel,
  output [4:0] Result
);

  wire [3:0] xor_4_out, xor_8_out;
  wire [4:0] not_1_out, not_2_out;

  xor xor_1 (xor_4_out[3], Input[4], Input[3]);
  xor xor_2 (xor_4_out[2], Input[3], Input[2]);
  assign not_1_out = ~{Input[0], Input[1], Input[2], Input[3], Input[4]};  // NOT_Gate not_1, 5 bits wide
  xor xor_3 (xor_4_out[1], Input[2], Input[1]);
  xor xor_4 (xor_4_out[0], Input[1], Input[0]);
  xor xor_5 (xor_8_out[3], not_1_out[3], not_1_out[4]);
  xor xor_6 (xor_8_out[2], not_1_out[2], xor_8_out[3]);
  xor xor_7 (xor_8_out[1], not_1_out[1], xor_8_out[2]);
  assign not_2_out = ~{Input[4], xor_4_out};  // NOT_Gate not_2, 5 bits wide
  xor xor_8 (xor_8_out[0], not_1_out[0], xor_8_out[1]);
  Multiplexer #(.width(5), .enable("false")) multiplexer_1 (
    .in0({not_2_out[0], not_2_out[1], not_2_out[2], not_2_out[3], not_2_out[4]}),
    .in1({not_1_out[4], xor_8_out}), .out(Result), .sel(Sel));
endmodule
